// Digital circuit CPU.dig as structural Verilog
module CPU (
  input  clk
);

  wire A_LD_CDATA, A_OUT_CDATA, ALU_COUT, ALU_NOUT, ALU_OUT_CDATA, ALU_VOUT, ALU_ZOUT, ALUA_LD_CDATA,
       ALUB_LD_CDATA, ALUOP_0, ALUOP_1, ALUOP_2, ALUP_LD_P, and_1_out, and_2_out, and_3_out, C,
       CDATA_TO_CADDRH, CDATA_TO_CADDRL, CVAL, IR_LD_XDATA, MARH_LD_CADDRH, MARL_LD_CADDRL, MBR_LD_CDATA,
       MBR_LD_XDATA, MBR_OUT_CDATA, MBR_OUT_XDATA, MEM_LD_XDATA, MEM_OUT_XDATA, multiplexer_5_out,
       multiplexer_6_out, multiplexer_7_out, multiplexer_8_out, N, not_1_out, NVAL, or_1_out, or_2_out,
       or_3_out, or_4_out, PC_INC, PC_LD, PC_LD_CVAL, PC_OUT_CADDR, PCADDL_c_o, PCH_LD_CADDRH, PCL_LD_CADDRL,
       PN_LD, PN_LD_NVAL, PV_LD, PV_LD_VVAL, PZ_LD, PZ_LD_ZVAL, STASH_LD_CDATA, STASH_OUT_CDATA, V, VVAL,
       X_LD_CDATA, X_OUT_CDATA, Y_LD_CDATA, Y_OUT_CDATA, Z, ZVAL;
  wire [3:0] ALUP_q;
  wire [7:0] A, ALUA, ALUB, ALUR, CDATA, driver_1_out, driver_2_out, IR, MARH, MARL, MBR, multiplexer_1_out,
       multiplexer_2_out, multiplexer_3_out, multiplexer_4_out, PCADDH_s, PCADDL_s, PCH, PCL, ROM_d, STASH,
       X, Y;

  Seven_Seg_Hex seven_seg_hex_1 (.d(MARH[7:4]), .dp(1'b0));
  Seven_Seg_Hex seven_seg_hex_2 (.d(A[7:4]), .dp(1'b0));
  Seven_Seg_Hex seven_seg_hex_3 (.d(MARL[7:4]), .dp(1'b0));
  Seven_Seg_Hex seven_seg_hex_4 (.d(MARH[3:0]), .dp(1'b0));
  Seven_Seg_Hex seven_seg_hex_5 (.d(A[3:0]), .dp(1'b0));
  Seven_Seg_Hex seven_seg_hex_6 (.d(MARL[3:0]), .dp(1'b0));
  Seven_Seg_Hex seven_seg_hex_7 (.d(X[3:0]), .dp(1'b0));
  Seven_Seg_Hex seven_seg_hex_8 (.d(X[7:4]), .dp(1'b0));
  Multiplexer #(.Bits(8)) multiplexer_1 (.sel(PC_INC), .in_0(driver_1_out), .in_1(PCADDH_s), .out(multiplexer_1_out));
  Seven_Seg_Hex seven_seg_hex_9 (.d(MBR[3:0]), .dp(1'b0));
  Seven_Seg_Hex seven_seg_hex_10 (.d(MBR[7:4]), .dp(1'b0));
  Seven_Seg_Hex seven_seg_hex_11 (.d(Y[3:0]), .dp(1'b0));
  Seven_Seg_Hex seven_seg_hex_12 (.d(Y[7:4]), .dp(1'b0));
  Seven_Seg_Hex seven_seg_hex_13 (.d(PCH[3:0]), .dp(1'b0));
  Seven_Seg_Hex seven_seg_hex_14 (.d(PCH[7:4]), .dp(1'b0));
  or or_1 (or_1_out, PC_INC, PCH_LD_CADDRH);
  Add #(.Bits(8)) PCADDH (.a(PCH), .b({8{1'b0}}), .c_i(PCADDL_c_o), .s(PCADDH_s));  // open: c_o
  Seven_Seg_Hex seven_seg_hex_15 (.d(PCL[3:0]), .dp(1'b0));
  Seven_Seg_Hex seven_seg_hex_16 (.d(PCL[7:4]), .dp(1'b0));
  Seven_Seg_Hex seven_seg_hex_17 (.d(ALUA[3:0]), .dp(1'b0));
  Seven_Seg_Hex seven_seg_hex_18 (.d(ALUA[7:4]), .dp(1'b0));
  Register #(.Bits(8)) u_PCH (.D(multiplexer_1_out), .C(clk), .en(or_1_out), .Q(PCH));
  Seven_Seg_Hex seven_seg_hex_19 (.d(IR[7:4]), .dp(1'b0));
  Seven_Seg_Hex seven_seg_hex_20 (.d(ALUB[7:4]), .dp(1'b0));
  LED led_1 (.in(N));
  Seven_Seg_Hex seven_seg_hex_21 (.d(IR[3:0]), .dp(1'b0));
  Seven_Seg_Hex seven_seg_hex_22 (.d(STASH[7:4]), .dp(1'b0));
  Seven_Seg_Hex seven_seg_hex_23 (.d(ALUB[3:0]), .dp(1'b0));
  Seven_Seg_Hex seven_seg_hex_24 (.d(ALUR[7:4]), .dp(1'b0));
  LED led_2 (.in(V));
  LED led_3 (.in(Z));
  assign driver_1_out = PC_OUT_CADDR ? PCH : 8'bz;  // Driver driver_1
  Seven_Seg_Hex seven_seg_hex_25 (.d(STASH[3:0]), .dp(1'b0));
  Seven_Seg_Hex seven_seg_hex_26 (.d(ALUR[3:0]), .dp(1'b0));
  LED led_4 (.in(C));
  Multiplexer #(.Bits(8)) multiplexer_2 (.sel(PC_INC), .in_0(driver_2_out), .in_1(PCADDL_s), .out(multiplexer_2_out));
  Multiplexer #(.Bits(8)) multiplexer_3 (.sel(PC_INC), .in_0(CDATA), .in_1(8'h1), .out(multiplexer_3_out));
  or or_2 (or_2_out, PC_INC, PCL_LD_CADDRL);
  Add #(.Bits(8)) PCADDL (.a(PCL), .b(multiplexer_3_out), .c_i(1'b0), .s(PCADDL_s), .c_o(PCADDL_c_o));
  Register #(.Bits(8)) u_PCL (.D(multiplexer_2_out), .C(clk), .en(or_2_out), .Q(PCL));
  Register #(.Bits(8)) MAR_H (.D(driver_1_out), .C(clk), .en(MARH_LD_CADDRH), .Q(MARH));
  assign driver_2_out = PC_OUT_CADDR ? PCL : 8'bz;  // Driver driver_2
  Register #(.Bits(8)) MAR_L (.D(driver_2_out), .C(clk), .en(MARL_LD_CADDRL), .Q(MARL));
  assign driver_2_out = CDATA_TO_CADDRL ? CDATA : 8'bz;  // Driver driver_3
  assign driver_1_out = CDATA_TO_CADDRH ? CDATA : 8'bz;  // Driver driver_4
  and and_1 (and_1_out, MARH[7], MEM_OUT_XDATA);
  Multiplexer #(.Bits(8)) multiplexer_4 (.sel(MBR_LD_CDATA), .in_0(ROM_d), .in_1(CDATA), .out(multiplexer_4_out));
  Register #(.Bits(8)) u_MBR (.D(multiplexer_4_out), .C(clk), .en(or_3_out), .Q(MBR));
  or or_3 (or_3_out, MBR_LD_CDATA, MBR_LD_XDATA);
  not not_1 (not_1_out, MARH[7]);
  ROM #(.AddrBits(14), .Bits(8)) ROM (.A({MARH[5:0], MARL}), .sel(and_1_out), .D(ROM_d));
  or or_4 (or_4_out, MEM_LD_XDATA, MEM_OUT_XDATA);
  assign ROM_d = MBR_OUT_XDATA ? MBR : 8'bz;  // Driver driver_5
  assign CDATA = MBR_OUT_CDATA ? MBR : 8'bz;  // Driver driver_6
  Register #(.Bits(8)) u_ALUB (.D(CDATA), .C(clk), .en(ALUB_LD_CDATA), .Q(ALUB));
  Multiplexer multiplexer_5 (.sel(PN_LD_NVAL), .in_0(ALU_NOUT), .in_1(NVAL), .out(multiplexer_5_out));
  Multiplexer multiplexer_6 (.sel(PV_LD_VVAL), .in_0(ALU_NOUT), .in_1(VVAL), .out(multiplexer_6_out));
  Multiplexer multiplexer_7 (.sel(PZ_LD_ZVAL), .in_0(ALU_NOUT), .in_1(ZVAL), .out(multiplexer_7_out));
  Multiplexer multiplexer_8 (.sel(PC_LD_CVAL), .in_0(ALU_NOUT), .in_1(CVAL), .out(multiplexer_8_out));
  and and_2 (and_2_out, or_4_out, not_1_out);
  and and_3 (and_3_out, MEM_LD_XDATA, clk);
  Register #(.Bits(4)) ALUP (.D({C, Z, V, N}), .C(clk), .en(ALUP_LD_P), .Q(ALUP_q));
  Register PN (.D(multiplexer_5_out), .C(clk), .en(PN_LD), .Q(N));
  Register PV (.D(multiplexer_6_out), .C(clk), .en(PV_LD), .Q(V));
  Register PZ (.D(multiplexer_7_out), .C(clk), .en(PZ_LD), .Q(Z));
  Register PC (.D(multiplexer_8_out), .C(clk), .en(PC_LD), .Q(C));
  Register #(.Bits(8)) u_IR (.D(ROM_d), .C(clk), .en(IR_LD_XDATA), .Q(IR));
  Register #(.Bits(8)) u_ALUA (.D(CDATA), .C(clk), .en(ALUA_LD_CDATA), .Q(ALUA));
  RAMSinglePortSel #(.AddrBits(14), .isProgramMemory("true"), .Bits(8)) RAM (
    .A({MARH[5:0], MARL}), .CS(and_2_out), .WE(and_3_out), .OE(MEM_OUT_XDATA), .D(ROM_d));
  ALU alu_1 (
    .A(ALUA), .B(ALUB), .OP({ALUOP_2, ALUOP_1, ALUOP_0}), .Nin(ALUP_q[0]), .Zin(ALUP_q[1]), .Cin(ALUP_q[2]),
    .Vin(ALUP_q[3]), .Out(ALUR), .Nout(ALU_NOUT), .Zout(ALU_VOUT), .Cout(ALU_ZOUT), .Vout(ALU_COUT));
  Register #(.Bits(8)) u_STASH (.D(CDATA), .C(clk), .en(STASH_LD_CDATA), .Q(STASH));
  assign CDATA = STASH_OUT_CDATA ? STASH : 8'bz;  // Driver driver_7
  assign CDATA = ALU_OUT_CDATA ? ALUR : 8'bz;  // Driver driver_8
  Control_Unit control_unit_1 (
    .Nin(N), .Vin(V), .Zin(Z), .Cin(C), .IRin(IR), .ClockIn(clk), .PC_OUT_CADDR(PC_OUT_CADDR),
    .MARH_LD_CADDRH(MARH_LD_CADDRH), .IR_LD_XDATA(IR_LD_XDATA), .PC_INC(PC_INC), .MBR_LD_XDATA(MBR_LD_XDATA),
    .MBR_OUT_CDATA(MBR_OUT_CDATA), .A_LD_CDATA(A_LD_CDATA), .MEM_OUT_XDATA(MEM_OUT_XDATA),
    .MEM_LD_XDATA(MEM_LD_XDATA), .MBR_OUT_XDATA(MBR_OUT_XDATA), .MBR_LD_CDATA(MBR_LD_CDATA),
    .A_OUT_CDATA(A_OUT_CDATA), .MARL_LD_CADDRL(MARL_LD_CADDRL), .CDATA_TO_CADDRH(CDATA_TO_CADDRH),
    .CDATA_TO_CADDRL(CDATA_TO_CADDRL), .STASH_LD_CDATA(STASH_LD_CDATA), .STASH_OUT_CDATA(STASH_OUT_CDATA),
    .PCL_LD_CADDRL(PCL_LD_CADDRL), .PCH_LD_CADDR(PCH_LD_CADDRH), .ALUA_LD_CDATA(ALUA_LD_CDATA),
    .ALUR_OUT_CDATA(ALU_OUT_CDATA), .ALUOP_0(ALUOP_0), .ALUOP_1(ALUOP_1), .ALUOP_2(ALUOP_2),
    .ALUB_LD_CDATA(ALUB_LD_CDATA), .X_LD_CDATA(X_LD_CDATA), .Y_LD_CDATA(Y_LD_CDATA),
    .X_OUT_CDATA(X_OUT_CDATA), .Y_OUT_CDATA(Y_OUT_CDATA), .PN_LD_NVAL(PN_LD_NVAL), .PV_LD_VVAL(PV_LD_VVAL),
    .PZ_LD_ZVAL(PZ_LD_ZVAL), .PC_LD_CVAL(PC_LD_CVAL), .NVAL(NVAL), .VVAL(VVAL), .ZVAL(ZVAL), .CVAL(CVAL),
    .PN_LD(PN_LD), .PV_LD(PV_LD), .PZ_LD(PZ_LD), .PC_LD(PC_LD), .ALUP_LD_P(ALUP_LD_P));
  Register #(.Bits(8)) u_A (.D(CDATA), .C(clk), .en(A_LD_CDATA), .Q(A));
  assign CDATA = A_OUT_CDATA ? A : 8'bz;  // Driver driver_9
  Register #(.Bits(8)) u_X (.D(CDATA), .C(clk), .en(X_LD_CDATA), .Q(X));
  assign CDATA = X_OUT_CDATA ? X : 8'bz;  // Driver driver_10
  Register #(.Bits(8)) u_Y (.D(CDATA), .C(clk), .en(Y_LD_CDATA), .Q(Y));
  assign CDATA = Y_OUT_CDATA ? Y : 8'bz;  // Driver driver_11

  // Other names for the same wires on the sheet: P0_Clock = clk; PC_LD_ADD = PC_INC

  // Notes on the sheet:
  //   clk: Hz: 100
  //   MAR
  //   A
  //   CADDRH Bus
  //   X
  //   MBR
  //   Y
  //   PC
  //   ALUA
  //   N
  //   V
  //   IR
  //   ALUB
  //   Z
  //   CADDRL Bus
  //   STASH
  //   ALUOUT
  //   C
  //   XADDR Bus
  //   High bit 
  //     set => ROM
  //     unset => RAM
  //   XDATA Bus
  //   CDATA Bus
  //   contents of ROM (hex, n*v repeats v):
  //   a9,42
endmodule
